# Fritzing sketch Proxectp (saved by Fritzing 1.0.6)
breadboards: 1

parts:
  Componente1 = Arduino Mega 2560 (Rev3)
  DHT1 = DHT22 Humidity and Temperature Sensor
  DHT2 = DHT22 Humidity and Temperature Sensor
  DHT3 = DHT22 Humidity and Temperature Sensor
  DS1 = DS18B20 1-Wire Temperature Sensor [part_number=DS18B20]
  DS2 = DS18B20 1-Wire Temperature Sensor [part_number=DS18B20]
  DS3 = DS18B20 1-Wire Temperature Sensor [part_number=DS18B20]
  Mod1 = KY-018 Photoresistor Module [package="Breakout board"]
  Mod2 = KY-018 Photoresistor Module [package="Breakout board"]
  Mod3 = KY-018 Photoresistor Module [package="Breakout board"]
  R1 = Rotary Potentiometer (Small) [maximum_resistance=10kΩ knob_status=50% power=0.5W package=THT]
  U1 = LCD-16X2 [package=lcd-16x2]
  R2 = Resistor [tolerance=±5% power=0.25W resistance=4700 package=THT]
  R3 = Resistor [tolerance=±5% power=0.25W resistance=4700 package=THT]
  R4 = Resistor [tolerance=±5% power=0.25W resistance=4700 package=THT]

nets:
  N1: Componente1.A0, Mod2.Vin
  N2: Componente1.A1, Mod3.Vin
  N3: Componente1.A2, Mod1.Vin
  N4: Componente1.D12_PWM, U1.RS
  N5: Componente1.D11_PWM, U1.E
  VDD: Componente1.5V, DHT1.VDD, DHT2.VDD, DHT3.VDD, DS1.VDD, DS2.VDD, DS3.VDD, Mod2.S, Mod3.S, R1.leg1, U1.VDD, U1.A, R2.Pin_0, R3.Pin_0, R4.Pin_0
  GND: Componente1.GND, DHT1.GND, DHT2.GND, DHT3.GND, DS1.GND, DS2.GND, DS3.GND, Mod1.S, Mod1.-, Mod2.-, Mod3.-, R1.leg2, U1.VSS, U1.R_W, U1.K
  N6: Componente1.D4_PWM, U1.DB4
  N7: Componente1.D5_PWM, U1.DB5
  N8: Componente1.D6_PWM, U1.DB6
  N9: Componente1.D7_PWM, U1.DB7
  N10: Componente1.D43, DS1.DQ, R2.Pin_1
  N11: Componente1.D45, DS3.DQ, R3.Pin_1
  N12: Componente1.D46, DHT1.DATA
  N13: Componente1.D47, DS2.DQ, R4.Pin_1
  N14: Componente1.D48, DHT2.DATA
  N15: Componente1.D50, DHT3.DATA
  N16: R1.wiper, U1.VO

custom parts:
  KY-018 Photoresistor Module: KY-018 Photoresistor module, used to measure light intensity. It can determine the presence or absence of light.
