# Fritzing sketch lus (saved by Fritzing 1.0.5)
breadboards: 1

parts:
  Mod1 = KY-018 Photoresistor Module [package="Breakout board"]
  Componente1 = Arduino Mega 2560 (Rev3)

nets:
  N1: Mod1.S, Componente1.A0
  VIN: Mod1.Vin, Componente1.5V
  N2: Mod1.-, Componente1.GND

custom parts:
  KY-018 Photoresistor Module: KY-018 Photoresistor module, used to measure light intensity. It can determine the presence or absence of light.
