# Fritzing sketch SensorPir (saved by Fritzing 1.0.5)
breadboards: 1

parts:
  PIR1 = PIR sensor
  Componente1 = Arduino Mega 2560 (Rev3)

nets:
  VDD: PIR1.VDD, Componente1.5V
  N1: PIR1.SIG, Componente1.D6_PWM
  GND: PIR1.GND, Componente1.GND
