# Fritzing sketch SensorTemp (saved by Fritzing 1.0.5)
breadboards: 1

parts:
  Componente1 = Arduino Mega 2560 (Rev3)
  DHT1 = DHT11 Humitidy and Temperature Sensor

nets:
  5V: Componente1.5V, DHT1.VDD
  GND: Componente1.GND, DHT1.GND
  N1: Componente1.D7_PWM, DHT1.DATA

custom parts:
  DHT11 Humitidy and Temperature Sensor: DHT11 Humidity and Temperature Sensor
