# Fritzing sketch sensores (saved by Fritzing 1.0.5)
circuit board: 8.46667cm x 5.64444cm
breadboards: 1

parts:
  Componente1 = Arduino Mega 2560 (Rev3)
  Mod1 = KY-018 Photoresistor Module [package="Breakout board"]
  PIR1 = PIR sensor
  DHT1 = DHT11 Humitidy and Temperature Sensor

nets:
  N1: Componente1.A0, Mod1.S
  GND: Componente1.GND, Mod1.-, PIR1.GND, DHT1.GND
  VDD: Componente1.5V, Mod1.Vin, PIR1.VDD, DHT1.VDD
  N2: Componente1.D6_PWM, PIR1.SIG
  N3: Componente1.D7_PWM, DHT1.DATA

custom parts:
  KY-018 Photoresistor Module: KY-018 Photoresistor module, used to measure light intensity. It can determine the presence or absence of light.
  DHT11 Humitidy and Temperature Sensor: DHT11 Humidity and Temperature Sensor
